// Logisim project control-logic.circ as structural Verilog: 1 circuit, main circuit control_logic
module control_logic (
  input  [31:0] Instruction,
  input  BrEq,
  input  BrLt,
  output PCSel,
  output RegWEn,
  output [2:0] ImmSel,
  output BrUn,
  output ASel,
  output BSel,
  output [3:0] ALUSel,
  output MemWEn,
  output [1:0] WBSel
);

  wire and_2_out, comparator_2_eq, IType;
  wire [2:0] priority_encoder_1_out;
  wire [5:0] and_1_out, bit_extender_1_out, bit_extender_2_out, ITypeInput, RomInput;
  wire [15:14] rom_1_data;

  ROM #(.addrWidth(6), .dataWidth(16)) rom_1 (
    .addr(RomInput), .data({rom_1_data, WBSel, MemWEn, ALUSel, BSel, ASel, BrUn, ImmSel, RegWEn}));
  assign bit_extender_1_out = {{5{IType}}, IType};  // Bit_Extender bit_extender_1
  Comparator #(.width(7)) comparator_1 (.a(Instruction[6:0]), .b(7'b0010011), .eq(IType));  // open: gt, lt
  Comparator #(.width(3)) comparator_2 (.a(Instruction[14:12]), .b(3'b101), .eq(comparator_2_eq));  // open: gt, lt
  assign and_1_out = 6'b001111 & bit_extender_1_out;  // AND_Gate and_1, 6 bits wide
  assign bit_extender_2_out = {{3{1'b0}}, Instruction[14:12]};  // Bit_Extender bit_extender_2
  Adder #(.width(6)) adder_1 (.a(and_1_out), .b(bit_extender_2_out), .out(ITypeInput), .cin(and_2_out));  // open: cout
  and and_2 (and_2_out, comparator_2_eq, Instruction[30]);
  Priority_Encoder priority_encoder_1 (
    .in0(IType), .in1(1'b0), .in2(1'b0), .in3(1'b0), .in4(1'b0), .in5(1'b0), .in6(1'b0), .in7(1'b0),
    .out(priority_encoder_1_out));  // open: en_in, gs, en_out
  Multiplexer #(.select(3), .width(6)) multiplexer_1 (
    .in0(ITypeInput), .out(RomInput), .sel(priority_encoder_1_out));  // open: in1, in2, in3, in4, in5, in6, in7

  assign PCSel = 1'b0;

  // Notes on the sheet:
  //   INPUTS to your circuit
  //   Connect ROM Input here ->
  //   contents of rom_1 (hex, n*v repeats v):
  //   15*0 1041 10d1 1141 1251 12d1 16c1 1351 13d1
  //   ROM FOR CONTROL LOGIC
  //   DON'T CHANGE THE LOCATIONS OF THE INPUTS AND OUTPUTS!
  //   This is only if you choose to do the ROM option
  //   CONNECT
  //   WIRE
  //   TO
  //   USE
  //   ROM
  //   OUTPUT from your circuit
  //   Reminder: If using ROM, use combinational logic for PCSel
endmodule
